// Logisim project Elevator_control.circ as structural Verilog: 8 circuits, main circuit main
module main (
  input  in_1,
  input  Enable,
  input  sleep_mode,
  input  in_4,
  input  in_5,
  input  in_6,
  input  in_7,
  input  in_8,
  input  password,
  input  in_10,
  input  Overload_check,
  output [5:0] UP_REG,
  output [5:0] DOWN_REG,
  output lift_on_off,
  output pass_correct
);

  wire _1D_out, _1U_out, _2_Hz_ticker_out, _2D_out, _2U_out, _3D_out, _3U_out, _4D_out, _4U_out, _5D_out,
       and_12_out, and_13_out, bot_with_thm_1_c0, bot_with_thm_1_c1, bot_with_thm_1_c2, bot_with_thm_1_c3,
       bot_with_thm_1_d0, bot_with_thm_1_d1, bot_with_thm_1_d2, bot_with_thm_1_d3, bot_with_thm_1_e0,
       bot_with_thm_1_e1, bot_with_thm_1_e2, bot_with_thm_1_e3, bot_with_thm_1_f0, bot_with_thm_1_f1,
       bot_with_thm_1_f2, bot_with_thm_1_f3, call_register_1_stop_flag, clk, clock_1_out, close_door_out,
       GU_out, j_k_ff_1_q, j_k_ff_1_qn, lift_shift_register_1_stop_flag, lift_shift_register_1_u_d_1_0,
       not_1_out, not_2_out, not_3_out, or_3_out, plus_1_hour_out, plus_1_minute_out, plus_1_second_out,
       priority_encoder_1_en_out, sleep_timing_check_1_lift_on_off, timer_1_enablen, timer_1_enables,
       top_1_c0, top_1_c1, top_1_c2, top_1_c3, top_1_d0, top_1_d1, top_1_d2, top_1_d3, top_1_e0, top_1_e1,
       top_1_e2, top_1_e3, top_1_f0, top_1_f1, top_1_f2, top_1_f3, ud_comparator_1_down,
       ud_comparator_1_stop, ud_comparator_1_up;
  wire [2:0] priority_encoder_1_out;
  wire [3:0] bcd_to_7sd_1_a, bcd_to_7sd_1_e, ud_encoder_1_dot, ud_encoder_1_g;
  wire [4:0] and_5_out;
  wire [5:0] bot_with_thm_1_hours, GR_out, lift_shift_register_1_gf, or_1_out, or_2_out,
       relative_position_comparator_1_down, relative_position_comparator_1_up, timer_1_hourn, timer_1_hours,
       timer_1_minn, timer_1_mins, timer_1_secn, timer_1_secs;
  wire [5:1] and_10_out;

  Button _5 (.out(GR_out[5]));
  Button _4 (.out(GR_out[4]));
  Button _3 (.out(GR_out[3]));
  Button _2 (.out(GR_out[2]));
  Button _1 (.out(GR_out[1]));
  Button GR (.out(GR_out[0]));
  and and_1 (and_5_out[4], _4U_out, pass_correct);
  and and_2 (and_5_out[3], _3U_out, pass_correct);
  and and_3 (and_5_out[2], _2U_out, pass_correct);
  and and_4 (and_5_out[1], _1U_out, pass_correct);
  and and_5 (and_5_out[0], GU_out, pass_correct);
  Relative_Position_Comparator relative_position_comparator_1 (
    .LIFT_IN(GR_out), .LIFT(lift_shift_register_1_gf), .DOWN(relative_position_comparator_1_down),
    .UP(relative_position_comparator_1_up));
  Button _4U (.out(_4U_out));
  Button _3U (.out(_3U_out));
  Button _2U (.out(_2U_out));
  Button _1U (.out(_1U_out));
  Button GU (.out(GU_out));
  password password_1 (
    .x6(in_4), .x5(in_5), .x4(in_6), .x3(in_7), .x2(in_8), .x1(password), .x0(in_10),
    .pass_correct(pass_correct));
  assign or_1_out = relative_position_comparator_1_down | {and_10_out, 1'b0};  // OR_Gate or_1, 6 bits wide
  assign or_2_out = relative_position_comparator_1_up | {1'b0, and_5_out};  // OR_Gate or_2, 6 bits wide
  Button _5D (.out(_5D_out));
  and and_6 (and_10_out[5], _5D_out, pass_correct);
  Button _4D (.out(_4D_out));
  and and_7 (and_10_out[4], _4D_out, pass_correct);
  Button _3D (.out(_3D_out));
  and and_8 (and_10_out[3], _3D_out, pass_correct);
  Button _2D (.out(_2D_out));
  and and_9 (and_10_out[2], _2D_out, pass_correct);
  Button _1D (.out(_1D_out));
  and and_10 (and_10_out[1], _1D_out, pass_correct);
  Call_Register call_register_1 (
    .DOWN(or_1_out), .UP(or_2_out), .LIFT(lift_shift_register_1_gf), .ud(lift_shift_register_1_u_d_1_0),
    .Clock(clk), .UP_REG(UP_REG), .DOWN_REG(DOWN_REG), .STOP_FLAG(call_register_1_stop_flag));
  Button close_door (.out(close_door_out));
  UD_Comparator ud_comparator_1 (
    .UP_REG(UP_REG), .DOWN_REG(DOWN_REG), .LIFT(lift_shift_register_1_gf), .Clock(clk),
    .UP(ud_comparator_1_up), .DOWN(ud_comparator_1_down), .STOP(ud_comparator_1_stop));
  or or_3 (or_3_out, ud_comparator_1_stop, j_k_ff_1_q);
  J_K_Flip_Flop j_k_ff_1 (
    .J(call_register_1_stop_flag), .clk(clk), .K(close_door_out), .Q(j_k_ff_1_q), .Qn(j_k_ff_1_qn));  // open: preset, en, reset
  LED door_open (.in(j_k_ff_1_q));
  Clock clock_1 (.out(clock_1_out));
  and and_11 (clk, clock_1_out, lift_on_off, not_1_out);
  not not_1 (not_1_out, Overload_check);
  LED Overload (.in(Overload_check));
  Lift_Shift_Register lift_shift_register_1 (
    .UP(ud_comparator_1_up), .DOWN(ud_comparator_1_down), .STOP(or_3_out),
    .u_d_1_0(lift_shift_register_1_u_d_1_0), .STOP_FLAG(lift_shift_register_1_stop_flag), .Clock(clk),
    .RESET(priority_encoder_1_en_out), ._5F(lift_shift_register_1_gf[5]), ._4F(lift_shift_register_1_gf[4]),
    ._3F(lift_shift_register_1_gf[3]), ._2F(lift_shift_register_1_gf[2]), ._1F(lift_shift_register_1_gf[1]),
    .GF(lift_shift_register_1_gf[0]));
  LED door_closed (.in(j_k_ff_1_qn));
  and and_12 (and_12_out, ud_encoder_1_g[3], lift_shift_register_1_u_d_1_0);
  LED up (.in(and_12_out));
  Clock _2_Hz_ticker (.out(_2_Hz_ticker_out));
  Timer timer_1 (
    .Clock(_2_Hz_ticker_out), .enable(Enable), .sec(plus_1_second_out), .min(plus_1_minute_out),
    .hour(plus_1_hour_out), .enableN(timer_1_enablen), .hourN(timer_1_hourn), .minN(timer_1_minn),
    .secN(timer_1_secn), .enableS(timer_1_enables), .hourS(timer_1_hours), .minS(timer_1_mins),
    .secS(timer_1_secs));
  Button plus_1_second (.out(plus_1_second_out));
  Button plus_1_minute (.out(plus_1_minute_out));
  Button plus_1_hour (.out(plus_1_hour_out));
  and and_13 (and_13_out, ud_encoder_1_g[3], not_2_out);
  not not_2 (not_2_out, lift_shift_register_1_u_d_1_0);
  LED down (.in(and_13_out));
  Priority_Encoder priority_encoder_1 (
    .in0(lift_shift_register_1_gf[0]), .in1(lift_shift_register_1_gf[1]), .in2(lift_shift_register_1_gf[2]),
    .in3(lift_shift_register_1_gf[3]), .in4(lift_shift_register_1_gf[4]), .in5(lift_shift_register_1_gf[5]),
    .out(priority_encoder_1_out), .en_in(1'b1), .en_out(priority_encoder_1_en_out));  // open: in6, in7, gs
  Top top_1 (
    .enable(timer_1_enablen), .hour(timer_1_hourn), .min(timer_1_minn), .sec(timer_1_secn), .f3(top_1_f3),
    .f2(top_1_f2), .f1(top_1_f1), .f0(top_1_f0), .e3(top_1_e3), .e2(top_1_e2), .e1(top_1_e1), .e0(top_1_e0),
    .d3(top_1_d3), .d2(top_1_d2), .d1(top_1_d1), .d0(top_1_d0), .c3(top_1_c3), .c2(top_1_c2), .c1(top_1_c1),
    .c0(top_1_c0));  // open: NO2
  _7_Segment_Display u_7_segment_display_1 (
    .g(top_1_f3), .f(top_1_f2), .a(top_1_f1), .b(top_1_f0), .e(bot_with_thm_1_f3), .d(bot_with_thm_1_f2),
    .c(bot_with_thm_1_f1), .dp(bot_with_thm_1_f0));
  bot_with_thm bot_with_thm_1 (
    .sec(timer_1_secs), .min(timer_1_mins), .hour(timer_1_hours), .enable(timer_1_enables),
    .f3(bot_with_thm_1_f3), .f2(bot_with_thm_1_f2), .f1(bot_with_thm_1_f1), .f0(bot_with_thm_1_f0),
    .e3(bot_with_thm_1_e3), .e2(bot_with_thm_1_e2), .e1(bot_with_thm_1_e1), .e0(bot_with_thm_1_e0),
    .d3(bot_with_thm_1_d3), .d2(bot_with_thm_1_d2), .d1(bot_with_thm_1_d1), .d0(bot_with_thm_1_d0),
    .c3(bot_with_thm_1_c3), .c2(bot_with_thm_1_c2), .c1(bot_with_thm_1_c1), .c0(bot_with_thm_1_c0),
    .hours(bot_with_thm_1_hours));  // open: NO2
  BCD_to_7SD bcd_to_7sd_1 (
    .in_1(priority_encoder_1_out), .a(bcd_to_7sd_1_a[0]), .b(bcd_to_7sd_1_a[1]), .c(bcd_to_7sd_1_a[2]),
    .d(bcd_to_7sd_1_a[3]), .e(bcd_to_7sd_1_e[0]), .f(bcd_to_7sd_1_e[1]), .g(bcd_to_7sd_1_e[2]),
    .h(bcd_to_7sd_1_e[3]));
  _7_Segment_Display u_7_segment_display_2 (
    .g(bcd_to_7sd_1_a[0]), .f(bcd_to_7sd_1_a[1]), .a(bcd_to_7sd_1_a[2]), .b(bcd_to_7sd_1_a[3]),
    .e(bcd_to_7sd_1_e[3]), .d(bcd_to_7sd_1_e[2]), .c(bcd_to_7sd_1_e[1]), .dp(bcd_to_7sd_1_e[0]));
  _7_Segment_Display u_7_segment_display_3 (
    .g(top_1_d3), .f(top_1_d2), .a(top_1_d1), .b(top_1_d0), .e(bot_with_thm_1_d3), .d(bot_with_thm_1_d2),
    .c(bot_with_thm_1_d1), .dp(bot_with_thm_1_d0));
  _7_Segment_Display u_7_segment_display_4 (
    .g(top_1_e3), .f(top_1_e2), .a(top_1_e1), .b(top_1_e0), .e(bot_with_thm_1_e3), .d(bot_with_thm_1_e2),
    .c(bot_with_thm_1_e1), .dp(bot_with_thm_1_e0));
  _7_Segment_Display u_7_segment_display_5 (
    .g(top_1_c3), .f(top_1_c2), .a(top_1_c1), .b(top_1_c0), .e(bot_with_thm_1_c3), .d(bot_with_thm_1_c2),
    .c(bot_with_thm_1_c1), .dp(bot_with_thm_1_c0));
  _7_Segment_Display u_7_segment_display_6 (
    .g(ud_encoder_1_g[0]), .f(ud_encoder_1_g[1]), .a(ud_encoder_1_g[2]), .b(ud_encoder_1_g[3]),
    .e(ud_encoder_1_dot[3]), .d(ud_encoder_1_dot[2]), .c(ud_encoder_1_dot[1]), .dp(ud_encoder_1_dot[0]));
  LED led_1 (.in(in_1));
  sleep_timing_check sleep_timing_check_1 (.in_1(bot_with_thm_1_hours), .lift_on_off(sleep_timing_check_1_lift_on_off));
  or or_4 (lift_on_off, sleep_timing_check_1_lift_on_off, not_3_out);
  UD_encoder ud_encoder_1 (
    .ud(lift_shift_register_1_u_d_1_0), .STOP(lift_shift_register_1_stop_flag), .g(ud_encoder_1_g[0]),
    .a(ud_encoder_1_g[1]), .b(ud_encoder_1_g[2]), .c(ud_encoder_1_g[3]), .dot(ud_encoder_1_dot[0]),
    .d(ud_encoder_1_dot[1]), .e(ud_encoder_1_dot[2]), .f(ud_encoder_1_dot[3]));
  not not_3 (not_3_out, sleep_mode);

  // Notes on the sheet:
  //   On if weight is greater than max capacity (480kg)
  //   Input from weight sensor
  //   On if weight is greater than minimum set (30kg)
  //   Light and Fan
endmodule

module BCD_to_7SD (
  input  [2:0] in_1,
  output a,
  output b,
  output c,
  output d,
  output e,
  output f,
  output g,
  output h
);

  wire decoder_1_out0, decoder_1_out1, decoder_1_out2, decoder_1_out3, decoder_1_out4, decoder_1_out5;

  Decoder #(.select(3)) decoder_1 (
    .out0(decoder_1_out0), .out1(decoder_1_out1), .out2(decoder_1_out2), .out3(decoder_1_out3),
    .out4(decoder_1_out4), .out5(decoder_1_out5), .sel(in_1));  // open: out6, out7, en
  nor nor_1 (a, decoder_1_out0, decoder_1_out1);
  nor nor_2 (b, decoder_1_out1, decoder_1_out2, decoder_1_out3);
  nor nor_3 (c, decoder_1_out1, decoder_1_out4);
  not not_1 (d, decoder_1_out5);
  not not_2 (f, decoder_1_out2);
  or or_1 (h, decoder_1_out0, decoder_1_out2);

  assign e = 1'b0;
  assign g = c;
endmodule

module Lift_Shift_Register (
  input  Clock,
  input  UP,
  input  DOWN,
  input  STOP,
  input  RESET,
  output _5F,
  output _4F,
  output _3F,
  output _2F,
  output u_d_1_0,
  output _1F,
  output STOP_FLAG,
  output GF
);

  wire and_1_out, and_2_out, and_3_out, j_k_ff_1_q, multiplexer_1_out, multiplexer_2_out, multiplexer_3_out,
       multiplexer_4_out, multiplexer_5_out, multiplexer_6_out, t_ff_1_q, t_ff_2_q, t_ff_3_q, t_ff_4_q,
       t_ff_5_q, t_ff_6_q;

  J_K_Flip_Flop j_k_ff_1 (
    .J(DOWN), .clk(Clock), .K(UP), .Q(j_k_ff_1_q), .Qn(u_d_1_0), .preset(RESET));  // open: en, reset
  and and_1 (and_1_out, t_ff_5_q, ~STOP_FLAG);  // AND_Gate
  Multiplexer #(.enable("false")) multiplexer_1 (.in0(_4F), .in1(1'b0), .out(multiplexer_1_out), .sel(j_k_ff_1_q));
  Multiplexer #(.enable("false")) multiplexer_2 (.in0(_3F), .in1(_5F), .out(multiplexer_2_out), .sel(j_k_ff_1_q));
  Multiplexer #(.enable("false")) multiplexer_3 (.in0(_2F), .in1(_4F), .out(multiplexer_3_out), .sel(j_k_ff_1_q));
  Multiplexer #(.enable("false")) multiplexer_4 (.in0(_1F), .in1(_3F), .out(multiplexer_4_out), .sel(j_k_ff_1_q));
  Multiplexer #(.enable("false")) multiplexer_5 (.in0(GF), .in1(_2F), .out(multiplexer_5_out), .sel(j_k_ff_1_q));
  Multiplexer #(.enable("false")) multiplexer_6 (.in0(1'b0), .in1(_1F), .out(multiplexer_6_out), .sel(j_k_ff_1_q));
  or or_1 (STOP_FLAG, and_3_out, STOP, and_2_out);
  D_Flip_Flop d_ff_1 (.clk(and_1_out), .D(multiplexer_1_out), .Q(_5F), .reset(RESET));  // open: Qn, preset, en
  D_Flip_Flop d_ff_2 (.clk(and_1_out), .D(multiplexer_2_out), .Q(_4F), .reset(RESET));  // open: Qn, preset, en
  D_Flip_Flop d_ff_3 (.clk(and_1_out), .D(multiplexer_3_out), .Q(_3F), .reset(RESET));  // open: Qn, preset, en
  D_Flip_Flop d_ff_4 (.clk(and_1_out), .D(multiplexer_4_out), .Q(_2F), .reset(RESET));  // open: Qn, preset, en
  D_Flip_Flop d_ff_5 (.clk(and_1_out), .D(multiplexer_5_out), .Q(_1F), .reset(RESET));  // open: Qn, preset, en
  D_Flip_Flop d_ff_6 (.clk(and_1_out), .D(multiplexer_6_out), .Q(GF), .preset(RESET));  // open: Qn, en, reset
  and and_2 (and_2_out, j_k_ff_1_q, GF);
  and and_3 (and_3_out, ~j_k_ff_1_q, _5F);  // AND_Gate
  T_Flip_Flop t_ff_1 (.clk(Clock), .T(1'b1), .Q(t_ff_1_q));  // open: Qn, preset, reset, en
  T_Flip_Flop t_ff_2 (.clk(t_ff_1_q), .T(1'b1), .Q(t_ff_2_q));  // open: Qn, preset, reset, en
  T_Flip_Flop t_ff_3 (.clk(t_ff_4_q), .T(1'b1), .Q(t_ff_3_q));  // open: Qn, preset, reset, en
  T_Flip_Flop t_ff_4 (.clk(t_ff_2_q), .T(1'b1), .Q(t_ff_4_q));  // open: Qn, preset, reset, en
  T_Flip_Flop t_ff_5 (.clk(t_ff_6_q), .T(1'b1), .Q(t_ff_5_q));  // open: Qn, preset, reset, en
  T_Flip_Flop t_ff_6 (.clk(t_ff_3_q), .T(1'b1), .Q(t_ff_6_q));  // open: Qn, preset, reset, en
endmodule

module UD_encoder (
  input  ud,
  input  STOP,
  output g,
  output a,
  output b,
  output c,
  output dot,
  output d,
  output e,
  output f
);

  nor nor_1 (a, ~ud, STOP);  // NOR_Gate
  not not_1 (c, STOP);
  not not_2 (g, a);

  assign b = 1'b0;
  assign d = c;
  assign dot = STOP;
  assign e = c;
  assign f = c;
endmodule

module Call_Register (
  input  [5:0] DOWN,
  input  Clock,
  input  [5:0] UP,
  input  [5:0] LIFT,
  input  ud,
  output [5:0] UP_REG,
  output [5:0] DOWN_REG,
  output STOP_FLAG
);

  wire bitselector_1_out, bitselector_2_out;
  wire [5:0] and_1_out, and_2_out, demultiplexer_1_out0, demultiplexer_1_out1;

  Demultiplexer #(.width(6), .enable("false")) demultiplexer_1 (
    .out0(demultiplexer_1_out0), .out1(demultiplexer_1_out1), .in(LIFT), .sel(ud));
  BitSelector #(.width(6)) bitselector_1 (.in(LIFT), .out(bitselector_1_out), .sel(3'b101));
  assign and_1_out = DOWN_REG & demultiplexer_1_out0;  // AND_Gate and_1, 6 bits wide
  J_K_Flip_Flop j_k_ff_1 (
    .J(DOWN[5]), .clk(Clock), .K(bitselector_1_out), .Q(DOWN_REG[5]));  // open: Qn, preset, en, reset
  J_K_Flip_Flop j_k_ff_2 (.J(DOWN[4]), .clk(Clock), .K(and_1_out[4]), .Q(DOWN_REG[4]));  // open: Qn, preset, en, reset
  J_K_Flip_Flop j_k_ff_3 (.J(DOWN[3]), .clk(Clock), .K(and_1_out[3]), .Q(DOWN_REG[3]));  // open: Qn, preset, en, reset
  J_K_Flip_Flop j_k_ff_4 (.J(DOWN[2]), .clk(Clock), .K(and_1_out[2]), .Q(DOWN_REG[2]));  // open: Qn, preset, en, reset
  J_K_Flip_Flop j_k_ff_5 (.J(DOWN[1]), .clk(Clock), .K(and_1_out[1]), .Q(DOWN_REG[1]));  // open: Qn, preset, en, reset
  J_K_Flip_Flop j_k_ff_6 (.J(DOWN[0]), .clk(Clock), .K(and_1_out[0]), .Q(DOWN_REG[0]));  // open: Qn, preset, en, reset
  assign and_2_out = UP_REG & demultiplexer_1_out1;  // AND_Gate and_2, 6 bits wide
  BitSelector #(.width(6)) bitselector_2 (.in(LIFT), .out(bitselector_2_out), .sel(3'b000));
  J_K_Flip_Flop j_k_ff_7 (.J(UP[5]), .clk(Clock), .K(and_2_out[5]), .Q(UP_REG[5]));  // open: Qn, preset, en, reset
  J_K_Flip_Flop j_k_ff_8 (.J(UP[4]), .clk(Clock), .K(and_2_out[4]), .Q(UP_REG[4]));  // open: Qn, preset, en, reset
  J_K_Flip_Flop j_k_ff_9 (.J(UP[3]), .clk(Clock), .K(and_2_out[3]), .Q(UP_REG[3]));  // open: Qn, preset, en, reset
  J_K_Flip_Flop j_k_ff_10 (.J(UP[2]), .clk(Clock), .K(and_2_out[2]), .Q(UP_REG[2]));  // open: Qn, preset, en, reset
  J_K_Flip_Flop j_k_ff_11 (.J(UP[1]), .clk(Clock), .K(and_2_out[1]), .Q(UP_REG[1]));  // open: Qn, preset, en, reset
  J_K_Flip_Flop j_k_ff_12 (
    .J(UP[0]), .clk(Clock), .K(bitselector_2_out), .Q(UP_REG[0]));  // open: Qn, preset, en, reset
  or or_1 (STOP_FLAG, and_2_out[0], and_2_out[1], and_2_out[2], and_2_out[3], and_2_out[4], and_2_out[5], and_1_out[0], and_1_out[1], and_1_out[2], and_1_out[3], and_1_out[4], and_1_out[5]);
endmodule

module UD_Comparator (
  input  Clock,
  input  [5:0] UP_REG,
  input  [5:0] DOWN_REG,
  input  [5:0] LIFT,
  output UP,
  output DOWN,
  output STOP
);

  wire comparator_1_gt, comparator_1_lt, comparator_2_gt, comparator_2_lt, decoder_1_out6, decoder_1_out7,
       decoder_2_out6, decoder_2_out7, nor_1_out, nor_2_out, nor_3_out, nor_4_out, nor_5_out, nor_6_out,
       nor_7_out, or_1_out, or_2_out, priority_encoder_1_en_out, priority_encoder_2_en_out, t_ff_1_q,
       t_ff_2_q, undriven, undriven_2, undriven_3, undriven_4;
  wire [2:0] priority_encoder_1_out, priority_encoder_2_out;
  wire [5:0] decoder_1_out0, decoder_2_out0;

  Priority_Encoder priority_encoder_1 (
    .in0(UP_REG[0]), .in1(UP_REG[1]), .in2(UP_REG[2]), .in3(UP_REG[3]), .in4(UP_REG[4]), .in5(UP_REG[5]),
    .in6(undriven), .in7(undriven_2), .out(priority_encoder_1_out), .en_in(1'b1),
    .en_out(priority_encoder_1_en_out));  // open: gs
  Priority_Encoder priority_encoder_2 (
    .in0(DOWN_REG[0]), .in1(DOWN_REG[1]), .in2(DOWN_REG[2]), .in3(DOWN_REG[3]), .in4(DOWN_REG[4]),
    .in5(DOWN_REG[5]), .in6(undriven_3), .in7(undriven_4), .out(priority_encoder_2_out), .en_in(1'b1),
    .en_out(priority_encoder_2_en_out));  // open: gs
  Decoder #(.select(3), .enable("false")) decoder_1 (
    .out0(decoder_1_out0[0]), .out1(decoder_1_out0[1]), .out2(decoder_1_out0[2]), .out3(decoder_1_out0[3]),
    .out4(decoder_1_out0[4]), .out5(decoder_1_out0[5]), .out6(decoder_1_out6), .out7(decoder_1_out7),
    .sel(priority_encoder_1_out));
  Decoder #(.select(3), .enable("false")) decoder_2 (
    .out0(decoder_2_out0[0]), .out1(decoder_2_out0[1]), .out2(decoder_2_out0[2]), .out3(decoder_2_out0[3]),
    .out4(decoder_2_out0[4]), .out5(decoder_2_out0[5]), .out6(decoder_2_out6), .out7(decoder_2_out7),
    .sel(priority_encoder_2_out));
  Comparator #(.width(6), .mode("unsigned")) comparator_1 (
    .a(decoder_1_out0), .b(LIFT), .gt(comparator_1_gt), .lt(comparator_1_lt));  // open: eq
  Comparator #(.width(6), .mode("unsigned")) comparator_2 (
    .a(decoder_2_out0), .b(LIFT), .gt(comparator_2_gt), .lt(comparator_2_lt));  // open: eq
  nor nor_1 (nor_1_out, priority_encoder_1_en_out, ~comparator_1_gt);  // NOR_Gate
  nor nor_2 (nor_2_out, ~comparator_1_lt, priority_encoder_1_en_out);  // NOR_Gate
  nor nor_3 (nor_3_out, priority_encoder_2_en_out, ~comparator_2_gt);  // NOR_Gate
  nor nor_4 (nor_4_out, ~comparator_2_lt, priority_encoder_2_en_out);  // NOR_Gate
  T_Flip_Flop t_ff_1 (.clk(Clock), .T(1'b1), .Q(t_ff_1_q));  // open: Qn, preset, reset, en
  or or_1 (or_1_out, nor_1_out, nor_3_out);
  or or_2 (or_2_out, nor_2_out, nor_4_out);
  T_Flip_Flop t_ff_2 (.clk(t_ff_1_q), .T(1'b1), .Q(t_ff_2_q));  // open: Qn, preset, reset, en
  nor nor_5 (nor_5_out, ~or_1_out, nor_6_out);  // NOR_Gate
  nor nor_6 (nor_6_out, nor_5_out, ~or_2_out);  // NOR_Gate
  nor nor_7 (nor_7_out, nor_5_out, nor_6_out);
  D_Flip_Flop d_ff_1 (.clk(t_ff_2_q), .D(nor_5_out), .Q(UP));  // open: Qn, preset, en, reset
  D_Flip_Flop d_ff_2 (.clk(t_ff_2_q), .D(nor_6_out), .Q(DOWN));  // open: Qn, preset, en, reset
  D_Flip_Flop d_ff_3 (.clk(t_ff_2_q), .D(nor_7_out), .Q(STOP));  // open: Qn, preset, en, reset
endmodule

module Relative_Position_Comparator (
  input  [5:0] LIFT_IN,
  input  [5:0] LIFT,
  output [5:0] DOWN,
  output [5:0] UP
);

  wire comparator_1_eq, comparator_1_gt, not_1_out;

  Demultiplexer #(.width(6)) demultiplexer_1 (
    .out0(DOWN), .out1(UP), .in(LIFT_IN), .sel(comparator_1_gt), .en(not_1_out));
  Comparator #(.width(6), .mode("unsigned")) comparator_1 (
    .a(LIFT_IN), .b(LIFT), .gt(comparator_1_gt), .eq(comparator_1_eq));  // open: lt
  not not_1 (not_1_out, comparator_1_eq);
endmodule

module password (
  input  x6,
  input  x5,
  input  x4,
  input  x3,
  input  x2,
  input  x1,
  input  x0,
  output pass_correct
);

  wire xnor_1_out, xnor_2_out, xnor_3_out, xnor_4_out, xnor_5_out, xnor_6_out, xnor_7_out;

  xnor xnor_1 (xnor_1_out, x6, 1'b1);
  xnor xnor_2 (xnor_2_out, x5, 1'b0);
  xnor xnor_3 (xnor_3_out, x4, 1'b0);
  xnor xnor_4 (xnor_4_out, x3, 1'b0);
  xnor xnor_5 (xnor_5_out, x2, 1'b1);
  xnor xnor_6 (xnor_6_out, x1, 1'b0);
  xnor xnor_7 (xnor_7_out, x0, 1'b1);
  and and_1 (pass_correct, xnor_1_out, xnor_2_out, xnor_3_out, xnor_4_out, xnor_5_out, xnor_6_out, xnor_7_out);
endmodule
